# Fritzing sketch SchematicV1 (saved by Fritzing 1.0.6)
breadboards: 1

parts:
  U1 = ESP32-38PinWide [part_number=ESP32-38PinWide]
  U2 = Voltage Regulator - 5V [package="TO220 [THT]"]
  C1 = Ceramic Capacitor [capacitance=100nF voltage=35V package="100 mil [THT, multilayer]"]
  C2 = Ceramic Capacitor [capacitance=100nF voltage=35V package="100 mil [THT, multilayer]"]
  BAT1 = Battery Holders [package=lipo-1100mAh]
  BAT2 = Battery Holders [package=lipo-1100mAh]
  Mod1 = KY-003 Hall Magnetic Sensor Module [package="Breakout board"]
  Mod2 = KY-003 Hall Magnetic Sensor Module [package="Breakout board"]

nets:
  N1: U1.GPIO34, Mod2.Vin
  N2: U1.GPIO35, Mod1.Vin
  N3: U1.VIN, U2.output_voltage, C1.1, Mod1.S, Mod2.S
  N4: U2.input_voltage, C2.1, BAT1.+
  N5: U2.GND, C1.0, C2.0, BAT2.-, Mod1.-, Mod2.-
  N6: BAT1.-, BAT2.+

custom parts:
  ESP32-38PinWide: Generic 38-Pin ESP32 with wide format (only access to one side of pins on a breadboard) based on Stephen Lilley's HiLetgo ESP-WROOM-32 ESP32 ESP-32S Development Board.
  KY-003 Hall Magnetic Sensor Module: KEYES KY-003 Arduino Hall Magnetic Sensor Module is a switch that will turn on/off in the presence of a magnetic field.
